# Fritzing sketch SchaltungEmpfaenger (saved by Fritzing 0.9.3b)
breadboards: 1

parts:
  U1 = NodeMCU V1.0
  IR1 = TSOP312.., 314.. [package=THT]
  S1 = Pushbutton [package="[THT]"]
  S2 = Pushbutton [package="[THT]"]
  S3 = Pushbutton [package="[THT]"]
  LED1 = RGB LED - (4 legs) [package="5 mm [THT]"]
  R1 = Resistor [tolerance=±5% resistance=220 package=THT]
  R2 = Resistor [tolerance=±5% resistance=10 package=THT]
  R3 = Resistor [tolerance=±5% resistance=10 package=THT]

nets:
  N1: U1.D1, R1.Pin_0
  N2: U1.D2, R2.Pin_1
  N3: U1.D3, R3.Pin_1
  N4: U1.D4, S1.Pin_1, S1.Pin_2
  N5: U1.3V3, IR1.Vs
  GND: U1.GND, IR1.GND, S1.Pin_3, S1.Pin_4, S2.Pin_3, S2.Pin_4, S3.Pin_3, S3.Pin_4, LED1.common_anode
  N6: U1.D5, S2.Pin_1, S2.Pin_2
  N7: U1.D6, S3.Pin_1, S3.Pin_2
  N8: U1.D7, IR1.Data
  N9: LED1.red_cathode, R1.Pin_1
  N10: LED1.green_cathode, R2.Pin_0
  N11: LED1.blue_cathode, R3.Pin_0

custom parts:
  NodeMCU V1.0: ESP8266 based NodeMCU
